// Logisim project Pipline Processor.circ as structural Verilog: 20 circuits, main circuit Pipeline Processor
module logicUnit (
  input  [15:0] A,
  input  [15:0] B,
  input  [2:0] Func,
  output [15:0] R
);

  wire [15:0] and_1_out, nor_1_out, or_1_out, shifter_1_out, shifter_2_out, shifter_3_out, shifter_4_out,
       xor_1_out;

  assign and_1_out = B & A;  // AND_Gate and_1, 16 bits wide
  assign or_1_out = B | A;  // OR_Gate or_1, 16 bits wide
  assign nor_1_out = ~(B | A);  // NOR_Gate nor_1, 16 bits wide
  assign xor_1_out = B ^ A;  // XOR_Gate xor_1, 16 bits wide
  Shifter #(.width(16)) shifter_1 (.in(A), .\dist (B[3:0]), .out(shifter_1_out));
  Shifter #(.width(16), .shift("lr")) shifter_2 (.in(A), .\dist (B[3:0]), .out(shifter_2_out));
  Shifter #(.width(16), .shift("ar")) shifter_3 (.in(A), .\dist (B[3:0]), .out(shifter_3_out));
  Shifter #(.width(16), .shift("rl")) shifter_4 (.in(A), .\dist (B[3:0]), .out(shifter_4_out));
  Multiplexer #(.select(3), .width(16), .enable("false")) multiplexer_1 (
    .in0(and_1_out), .in1(or_1_out), .in2(nor_1_out), .in3(xor_1_out), .in4(shifter_1_out),
    .in5(shifter_2_out), .in6(shifter_3_out), .in7(shifter_4_out), .out(R), .sel(Func));
endmodule

module ArithUnit (
  input  [15:0] A,
  input  [15:0] B,
  input  [2:0] func,
  output zeroFlag,
  output [15:0] R
);

  wire comparator_1_eq, comparator_1_lt, comparator_2_eq, comparator_2_lt, or_1_out, or_2_out;
  wire [15:0] adder_1_out, bit_extender_1_out, bit_extender_2_out, bit_extender_3_out, bit_extender_4_out,
       subtractor_1_out;

  Comparator #(.width(16)) comparator_1 (.a(A), .b(B), .eq(comparator_1_eq), .lt(comparator_1_lt));  // open: gt
  Comparator #(.width(16), .mode("unsigned")) comparator_2 (
    .a(A), .b(B), .eq(comparator_2_eq), .lt(comparator_2_lt));  // open: gt
  Adder #(.width(16)) adder_1 (.a(A), .b(B), .out(adder_1_out), .cin(1'b0));  // open: cout
  Subtractor #(.width(16)) subtractor_1 (.a(A), .b(B), .out(subtractor_1_out), .bin(1'b0));  // open: bout
  or or_1 (or_1_out, comparator_2_eq, comparator_2_lt);
  or or_2 (or_2_out, comparator_1_eq, comparator_1_lt);
  assign bit_extender_1_out = {{15{1'b0}}, comparator_1_lt};  // Bit_Extender bit_extender_1
  assign bit_extender_2_out = {{15{1'b0}}, comparator_2_lt};  // Bit_Extender bit_extender_2
  assign bit_extender_3_out = {{15{1'b0}}, or_2_out};  // Bit_Extender bit_extender_3
  assign bit_extender_4_out = {{15{1'b0}}, or_1_out};  // Bit_Extender bit_extender_4
  Multiplexer #(.select(3), .width(16), .enable("false")) multiplexer_1 (
    .in0(adder_1_out), .in1(subtractor_1_out), .in2(bit_extender_1_out), .in3(bit_extender_2_out),
    .in4(bit_extender_3_out), .in5(bit_extender_4_out), .in6(A), .in7(A), .out(R), .sel(func));
  nor nor_1 (zeroFlag, subtractor_1_out[0], subtractor_1_out[1], subtractor_1_out[2], subtractor_1_out[3], subtractor_1_out[4], subtractor_1_out[5], subtractor_1_out[6], subtractor_1_out[7], subtractor_1_out[8], subtractor_1_out[9], subtractor_1_out[10], subtractor_1_out[11], subtractor_1_out[12], subtractor_1_out[13], subtractor_1_out[14], subtractor_1_out[15]);
endmodule

module ALU (
  input  [15:0] in_1,
  input  [15:0] in_2,
  input  [3:0] Code,
  output [15:0] out_4,
  output zeroFlag
);

  wire [15:0] arithunit_1_r, logicunit_1_r;

  logicUnit logicunit_1 (.R(logicunit_1_r), .A(in_1), .B(in_2), .Func(Code[3:1]));
  ArithUnit arithunit_1 (.A(in_1), .B(in_2), .zeroFlag(zeroFlag), .R(arithunit_1_r), .func(Code[3:1]));
  Multiplexer #(.width(16), .enable("false")) multiplexer_1 (
    .in0(logicunit_1_r), .in1(arithunit_1_r), .out(out_4), .sel(Code[0]));
endmodule

// ALU Control Unit
module ALUControlUnit (
  input  [2:0] Func,
  input  [2:0] ALUOp,
  output [3:0] Code
);

  Multiplexer #(.select(3), .width(4), .enable("false")) multiplexer_1 (
    .in0({Func, 1'b0}), .in1({Func, 1'b1}), .in2(4'b0001), .in3(4'b0000), .in4(4'b0010), .out(Code),
    .sel(ALUOp));  // open: in5, in6, in7
endmodule

module RegisterFile (
  input  clk,
  input  [15:0] Data,
  input  [2:0] A,
  input  Write,
  input  [2:0] Rd,
  input  [2:0] B,
  output [15:0] BusA,
  output [15:0] BusB,
  output [15:0] R0,
  output [15:0] R1,
  output [15:0] R2,
  output [15:0] R3,
  output [15:0] R4,
  output [15:0] R5,
  output [15:0] R6,
  output [15:0] R7
);

  wire demultiplexer_1_out0, demultiplexer_1_out1, demultiplexer_1_out2, demultiplexer_1_out3,
       demultiplexer_1_out4, demultiplexer_1_out5, demultiplexer_1_out6, demultiplexer_1_out7;

  Demultiplexer #(.select(3), .enable("false")) demultiplexer_1 (
    .out0(demultiplexer_1_out0), .out1(demultiplexer_1_out1), .out2(demultiplexer_1_out2),
    .out3(demultiplexer_1_out3), .out4(demultiplexer_1_out4), .out5(demultiplexer_1_out5),
    .out6(demultiplexer_1_out6), .out7(demultiplexer_1_out7), .in(Write), .sel(Rd));
  Register #(.width(16)) register_1 (.D({16{1'b0}}), .en(demultiplexer_1_out0), .Q(R0), .clk(clk));  // open: clr
  Register #(.width(16)) u_R1 (.D(Data), .en(demultiplexer_1_out1), .Q(R1), .clk(clk));  // open: clr
  Register #(.width(16)) u_R2 (.D(Data), .en(demultiplexer_1_out2), .Q(R2), .clk(clk));  // open: clr
  Register #(.width(16)) u_R3 (.D(Data), .en(demultiplexer_1_out3), .Q(R3), .clk(clk));  // open: clr
  Register #(.width(16)) u_R4 (.D(Data), .en(demultiplexer_1_out4), .Q(R4), .clk(clk));  // open: clr
  Register #(.width(16)) u_R5 (.D(Data), .en(demultiplexer_1_out5), .Q(R5), .clk(clk));  // open: clr
  Register #(.width(16)) u_R6 (.D(Data), .en(demultiplexer_1_out6), .Q(R6), .clk(clk));  // open: clr
  Register #(.width(16)) u_R7 (.D(Data), .en(demultiplexer_1_out7), .Q(R7), .clk(clk));  // open: clr
  Multiplexer #(.select(3), .width(16), .enable("false")) multiplexer_1 (
    .in0(R0), .in1(R1), .in2(R2), .in3(R3), .in4(R4), .in5(R5), .in6(R6), .in7(R7), .out(BusA), .sel(A));
  Multiplexer #(.select(3), .width(16), .enable("false")) multiplexer_2 (
    .in0(R0), .in1(R1), .in2(R2), .in3(R3), .in4(R4), .in5(R5), .in6(R6), .in7(R7), .out(BusB), .sel(B));
endmodule

// PC Value
module PC_Value (
  input  [15:0] busA,
  input  [1:0] PC2,
  input  [5:0] offset_br,
  input  clk,
  input  [11:0] jump_0_11,
  input  zero_flag,
  input  bne,
  input  beq,
  output [11:0] PC_plus_1,
  output [11:0] PC_value
);

  wire and_1_out, and_2_out, or_1_out;
  wire [11:0] adder_1_out, bit_extender_1_out, bit_extender_2_out, multiplexer_1_out, multiplexer_2_out;

  branchOrNot branchornot_1 ();  // open: J, zero_flag, bne, beq, MUXSel
  assign bit_extender_1_out = {{6{offset_br[5]}}, offset_br};  // Bit_Extender bit_extender_1
  Adder #(.width(12)) adder_1 (.a(bit_extender_1_out), .b(PC_plus_1), .out(adder_1_out));  // open: cin, cout
  Multiplexer #(.width(12), .enable("false")) multiplexer_1 (
    .in0(PC_plus_1), .in1(adder_1_out), .out(multiplexer_1_out), .sel(or_1_out));
  or or_1 (or_1_out, and_1_out, and_2_out);
  and and_1 (and_1_out, ~zero_flag, bne);  // AND_Gate
  and and_2 (and_2_out, zero_flag, beq);
  Bit_Extender #(.in_width(16), .out_width(12)) bit_extender_2 (.in(busA), .out(bit_extender_2_out));
  Multiplexer #(.select(2), .width(12), .enable("false")) multiplexer_2 (
    .in0(multiplexer_1_out), .in1(bit_extender_2_out), .in2(jump_0_11), .out(multiplexer_2_out), .sel(PC2));  // open: in3
  Register #(.width(12)) register_1 (.D(multiplexer_2_out), .Q(PC_value), .clk(clk));  // open: en, clr
  Adder #(.width(12)) adder_2 (.a(12'h1), .b(PC_value), .out(PC_plus_1));  // open: cin, cout
endmodule

// Control Unit
module ControlUnit (
  input  [3:0] OP,
  input  [1:0] JRJALR,
  output [1:0] Rd,
  output [2:0] Flush,
  output sec,
  output [1:0] Dest,
  output [2:0] ALUOP,
  output beq,
  output bne,
  output [1:0] PC2,
  output MemWrt,
  output MemRead,
  output RegWrt
);

  wire and_1_out, and_3_out, and_4_out, and_5_out, and_6_out, and_7_out, and_8_out, and_13_out, and_14_out,
       and_15_out, and_16_out, not_1_out, not_2_out, not_3_out, not_4_out, not_5_out, not_6_out, not_7_out,
       not_8_out, not_9_out, not_10_out, not_11_out, not_12_out, not_13_out, not_14_out, not_15_out,
       not_16_out, not_17_out, not_18_out, not_19_out, not_20_out, not_21_out, not_22_out;
  wire [3:0] bit_extender_1_out, bit_extender_2_out;

  flushing flushing_1 (.OP(OP), .JR(bit_extender_1_out), .JALR(bit_extender_2_out), .Flush(Flush));
  assign bit_extender_1_out = {{3{1'b0}}, JRJALR[0]};  // Bit_Extender bit_extender_1
  assign bit_extender_2_out = {{3{1'b0}}, JRJALR[1]};  // Bit_Extender bit_extender_2
  aluOP aluop_1 (.OP3(OP[3]), .OP2(OP[2]), .OP1(OP[1]), .OP0(OP[0]), .ALU2(ALUOP[2]), .ALU1(ALUOP[1]), .ALU0(ALUOP[0]));
  not not_1 (not_1_out, OP[1]);
  not not_2 (not_2_out, JRJALR[1]);
  not not_3 (not_3_out, OP[0]);
  and and_1 (and_1_out, OP[3], OP[1]);
  or or_1 (sec, OP[1], OP[3]);
  not not_4 (not_4_out, OP[3]);
  not not_5 (not_5_out, OP[1]);
  not not_6 (not_6_out, OP[3]);
  not not_7 (not_7_out, OP[1]);
  not not_8 (not_8_out, OP[0]);
  not not_9 (not_9_out, OP[1]);
  not not_10 (not_10_out, OP[0]);
  not not_11 (not_11_out, OP[1]);
  and and_2 (PC2[1], OP[3], OP[0]);
  or or_2 (PC2[0], JRJALR[1], JRJALR[0]);
  not not_12 (not_12_out, OP[3]);
  not not_13 (not_13_out, OP[2]);
  not not_14 (not_14_out, OP[3]);
  not not_15 (not_15_out, OP[2]);
  not not_16 (not_16_out, OP[0]);
  not not_17 (not_17_out, OP[3]);
  not not_18 (not_18_out, OP[2]);
  not not_19 (not_19_out, OP[1]);
  not not_20 (not_20_out, JRJALR[0]);
  not not_21 (not_21_out, OP[2]);
  not not_22 (not_22_out, OP[0]);
  and and_3 (and_3_out, not_1_out, not_2_out);
  and and_4 (and_4_out, OP[3], not_3_out);
  or or_3 (Rd[0], JRJALR[1], and_1_out);
  and and_5 (and_5_out, not_4_out, not_5_out);
  and and_6 (and_6_out, OP[3], OP[0]);
  and and_7 (and_7_out, not_6_out, not_7_out);
  and and_8 (and_8_out, OP[3], OP[1], not_8_out);
  and and_9 (beq, OP[2], not_9_out, not_10_out);
  and and_10 (bne, OP[2], not_11_out, OP[0]);
  and and_11 (MemWrt, not_12_out, not_13_out, OP[1], OP[0]);
  and and_12 (MemRead, not_14_out, not_15_out, OP[1], not_16_out);
  and and_13 (and_13_out, not_17_out, not_18_out, not_19_out, not_20_out);
  and and_14 (and_14_out, not_21_out, not_22_out);
  and and_15 (and_15_out, OP[2], OP[1]);
  and and_16 (and_16_out, OP[3], OP[1]);
  or or_4 (Rd[1], and_3_out, OP[2], and_4_out);
  or or_5 (Dest[1], and_5_out, and_6_out);
  or or_6 (Dest[0], and_7_out, and_8_out);
  or or_7 (RegWrt, and_13_out, and_14_out, and_15_out, and_16_out);
endmodule

module Jout2 (
  input  [3:0] Op,
  input  [2:0] Func,
  output [1:0] JRJAR
);

  wire not_1_out, not_2_out, not_3_out, not_4_out, not_5_out, not_6_out, not_7_out;

  not not_1 (not_1_out, Op[3]);
  not not_2 (not_2_out, Op[2]);
  not not_3 (not_3_out, Op[1]);
  not not_4 (not_4_out, Func[0]);
  not not_5 (not_5_out, Op[3]);
  not not_6 (not_6_out, Op[2]);
  not not_7 (not_7_out, Op[1]);
  and and_1 (JRJAR[0], not_1_out, not_2_out, not_3_out, Op[0], Func[2], Func[1], not_4_out);
  and and_2 (JRJAR[1], not_5_out, not_6_out, not_7_out, Op[0], Func[2], Func[1], Func[0]);
endmodule

module PROCESSOR (
  output [15:0] R0,
  output [15:0] R1,
  output [15:0] R2,
  output [15:0] R3,
  output [15:0] R4,
  output [15:0] R5,
  output [15:0] R6,
  output [15:0] R7
);

  wire _0, _1, _2, _3, _4, _5, _6, _7, _8, _9, _10, _11, _12, _13, _14, _15, beq, bne, clk,
       controlunit_1_regwrt, MemRe, MemWrt, Sec, z_flagg;
  wire [1:0] Dest, jout2_1_jrjar, PC2, Rd;
  wire [2:0] ALuOp, multiplexer_1_out;
  wire [3:0] alucontrolunit_1_code;
  wire [11:0] bit_extender_4_out, pc_value_1_pc_plus_1, pc_value_1_pc_value;
  wire [15:0] alu_1_out_4, bit_extender_2_out, bit_extender_3_out, jr, LUP, multiplexer_2_out,
       multiplexer_3_out, pc_plusOne, ram_1_data, registerfile_1_busb;

  PC_Value pc_value_1 (
    .busA(jr), .PC2(PC2), .offset_br({_5, _4, _3, _2, _1, _0}),
    .jump_0_11({_11, _10, _9, _8, _7, _6, _5, _4, _3, _2, _1, _0}), .zero_flag(z_flagg), .bne(bne),
    .beq(beq), .PC_plus_1(pc_value_1_pc_plus_1), .PC_value(pc_value_1_pc_value), .clk(clk));
  assign pc_plusOne = {{4{1'b0}}, pc_value_1_pc_plus_1};  // Bit_Extender bit_extender_1
  ROM #(.addrWidth(12), .dataWidth(16)) rom_1 (
    .addr(pc_value_1_pc_value), .data({_15, _14, _13, _12, _11, _10, _9, _8, _7, _6, _5, _4, _3, _2, _1, _0}));  // open: sel
  Clock clock_1 (.out(clk));
  Multiplexer #(.select(2), .width(3), .enable("false")) multiplexer_1 (
    .in0({_8, _7, _6}), .in1(3'b001), .in2(3'b111), .in3({_5, _4, _3}), .out(multiplexer_1_out), .sel(Dest));
  Jout2 jout2_1 (.Op({_15, _14, _13, _12}), .Func({_2, _1, _0}), .JRJAR(jout2_1_jrjar));
  assign bit_extender_2_out = {{4{1'b0}}, {_11, _10, _9, _8, _7, _6, _5, _4, _3, _2, _1, _0}};  // Bit_Extender bit_extender_2
  assign bit_extender_3_out = {{10{_5}}, {_5, _4, _3, _2, _1, _0}};  // Bit_Extender bit_extender_3
  Shifter #(.width(16)) shifter_1 (.in(bit_extender_2_out), .\dist (4'b0100), .out(LUP));
  RegisterFile registerfile_1 (
    .clk(clk), .Data(multiplexer_3_out), .Write(controlunit_1_regwrt), .Rd(multiplexer_1_out), .BusA(jr),
    .A({_11, _10, _9}), .BusB(registerfile_1_busb), .B({_8, _7, _6}), .R0(R0), .R1(R1), .R2(R2), .R3(R3),
    .R4(R4), .R5(R5), .R6(R6), .R7(R7));
  ALUControlUnit alucontrolunit_1 (.Func({_2, _1, _0}), .ALUOp(ALuOp), .Code(alucontrolunit_1_code));
  ControlUnit controlunit_1 (
    .OP({_15, _14, _13, _12}), .Rd(Rd), .sec(Sec), .JRJALR(jout2_1_jrjar), .Dest(Dest), .ALUOP(ALuOp),
    .beq(beq), .bne(bne), .PC2(PC2), .MemWrt(MemWrt), .MemRead(MemRe), .RegWrt(controlunit_1_regwrt));  // open: Flush
  Multiplexer #(.width(16), .enable("false")) multiplexer_2 (
    .in0(registerfile_1_busb), .in1(bit_extender_3_out), .out(multiplexer_2_out), .sel(Sec));
  ALU alu_1 (
    .in_1(jr), .in_2(multiplexer_2_out), .Code(alucontrolunit_1_code), .out_4(alu_1_out_4), .zeroFlag(z_flagg));
  Bit_Extender #(.in_width(16), .out_width(12)) bit_extender_4 (.in(alu_1_out_4), .out(bit_extender_4_out));
  RAM #(.addrWidth(12), .dataWidth(16), .bus("separate")) ram_1 (
    .addr(bit_extender_4_out), .din(registerfile_1_busb), .data(ram_1_data), .str(MemWrt), .clk(clk),
    .ld(MemRe));  // open: sel, clr
  Multiplexer #(.select(2), .width(16), .enable("false")) multiplexer_3 (
    .in0(ram_1_data), .in1(pc_plusOne), .in2(alu_1_out_4), .in3(LUP), .out(multiplexer_3_out), .sel(Rd));

  // Other names for the same wires on the sheet: j[11:0] = {_11, _10, _9, _8, _7, _6, _5, _4, _3, _2, _1, _0};
  //   offset[5:0] = {_5, _4, _3, _2, _1, _0}

  // Notes on the sheet:
  //   contents of rom_1 (hex, n*v repeats v):
  //   a384 8354 35b 2040 2081 20c2 890a 1921 1520 14f2 4182 1290 403b 3100 b012 55c 1b68 403f 4e9 2040
  //   2285 22c6 4e0 3100 1e06
endmodule

module aluOP (
  input  OP3,
  input  OP2,
  input  OP1,
  input  OP0,
  output ALU2,
  output ALU1,
  output ALU0
);

  wire and_2_out, and_3_out, and_4_out, and_5_out, not_1_out, not_2_out, not_3_out, not_4_out;

  and and_1 (ALU2, OP2, OP0);
  not not_1 (not_1_out, OP2);
  not not_2 (not_2_out, OP0);
  not not_3 (not_3_out, OP1);
  not not_4 (not_4_out, OP0);
  and and_2 (and_2_out, not_1_out, OP1);
  and and_3 (and_3_out, OP2, not_2_out);
  and and_4 (and_4_out, not_3_out, OP0);
  and and_5 (and_5_out, OP2, not_4_out);
  or or_1 (ALU1, and_2_out, and_3_out, OP3);
  or or_2 (ALU0, and_4_out, and_5_out);
endmodule

module IF_ID_Reg (
  input  clk,
  input  IF_Flush,
  input  [15:0] Inst,
  input  [11:0] N_Pc,
  input  IF_ID_Wrt,
  output [15:0] Inst_2,
  output [11:0] N_Pc_2
);

  wire [11:0] multiplexer_2_out;
  wire [15:0] multiplexer_1_out;

  Multiplexer #(.width(16), .enable("false")) multiplexer_1 (
    .in0(Inst), .in1({16{1'b0}}), .out(multiplexer_1_out), .sel(IF_Flush));
  Multiplexer #(.width(12), .enable("false")) multiplexer_2 (
    .in0(N_Pc), .in1({12{1'b0}}), .out(multiplexer_2_out), .sel(IF_Flush));
  Register #(.width(16)) register_1 (.D(multiplexer_1_out), .en(IF_ID_Wrt), .Q(Inst_2), .clk(clk));  // open: clr
  Register #(.width(12)) register_2 (.D(multiplexer_2_out), .en(IF_ID_Wrt), .Q(N_Pc_2), .clk(clk));  // open: clr
endmodule

module ID_EX_Reg (
  input  clk,
  input  [15:0] A,
  input  [15:0] B,
  input  [2:0] Rd1,
  input  [15:0] Imm,
  input  [2:0] Rs,
  input  [2:0] Rt,
  input  [11:0] EX_ctrl_signals,
  input  [15:0] N_PC,
  input  [15:0] LUI,
  output [15:0] A_2,
  output [15:0] B_2,
  output [2:0] Rd1_2,
  output [15:0] Imm_2,
  output [2:0] Rs_2,
  output [2:0] Rt_2,
  output [11:0] EX_ctrl_signals_2,
  output [15:0] N_PC_2,
  output [15:0] LUI_2
);

  Register #(.width(16)) register_1 (.D(A), .en(1'b1), .Q(A_2), .clk(clk));  // open: clr
  Register #(.width(16)) register_2 (.D(B), .en(1'b1), .Q(B_2), .clk(clk));  // open: clr
  Register #(.width(3)) register_3 (.D(Rd1), .en(1'b1), .Q(Rd1_2), .clk(clk));  // open: clr
  Register #(.width(16)) register_4 (.D(Imm), .en(1'b1), .Q(Imm_2), .clk(clk));  // open: clr
  Register #(.width(3)) register_5 (.D(Rs), .en(1'b1), .Q(Rs_2), .clk(clk));  // open: clr
  Register #(.width(3)) register_6 (.D(Rt), .en(1'b1), .Q(Rt_2), .clk(clk));  // open: clr
  Register #(.width(12)) register_7 (.D(EX_ctrl_signals), .en(1'b1), .Q(EX_ctrl_signals_2), .clk(clk));  // open: clr
  Register #(.width(16)) register_8 (.D(N_PC), .en(1'b1), .Q(N_PC_2), .clk(clk));  // open: clr
  Register #(.width(16)) register_9 (.D(LUI), .en(1'b1), .Q(LUI_2), .clk(clk));  // open: clr
endmodule

module EX_DM_Reg (
  input  clk,
  input  [15:0] ALU_Result,
  input  [2:0] Rd2,
  input  [15:0] Bus_B,
  input  [4:0] EX_Dm_ctrl,
  input  [15:0] N_PC,
  input  [15:0] LUI,
  output [15:0] ALU_Result_2,
  output [2:0] Rd2_2,
  output [15:0] Bus_B_2,
  output [4:0] EX_Dm_ctrl_2,
  output [15:0] N_PC_2,
  output [15:0] LUI_2
);

  Register #(.width(16)) register_1 (.D(ALU_Result), .en(1'b1), .Q(ALU_Result_2), .clk(clk));  // open: clr
  Register #(.width(3)) register_2 (.D(Rd2), .en(1'b1), .Q(Rd2_2), .clk(clk));  // open: clr
  Register #(.width(16)) register_3 (.D(Bus_B), .en(1'b1), .Q(Bus_B_2), .clk(clk));  // open: clr
  Register #(.width(5)) register_4 (.D(EX_Dm_ctrl), .en(1'b1), .Q(EX_Dm_ctrl_2), .clk(clk));  // open: clr
  Register #(.width(16)) register_5 (.D(N_PC), .en(1'b1), .Q(N_PC_2), .clk(clk));  // open: clr
  Register #(.width(16)) register_6 (.D(LUI), .en(1'b1), .Q(LUI_2), .clk(clk));  // open: clr
endmodule

module DM_WB_Reg (
  input  clk,
  input  [15:0] Data_Wrt,
  input  [2:0] Rd3,
  input  Reg_wrt,
  output [15:0] Data_Wrt_2,
  output [2:0] Rd3_2,
  output Reg_wrt_2
);

  Register #(.width(16)) register_1 (.D(Data_Wrt), .en(1'b1), .Q(Data_Wrt_2), .clk(clk));  // open: clr
  Register #(.width(3)) register_2 (.D(Rd3), .en(1'b1), .Q(Rd3_2), .clk(clk));  // open: clr
  Register #(.width(1)) register_3 (.D(Reg_wrt), .en(1'b1), .Q(Reg_wrt_2), .clk(clk));  // open: clr
endmodule

module Pipeline_Processor (
  output [15:0] R0,
  output [15:0] R1,
  output [15:0] R2,
  output [15:0] R3,
  output [15:0] R4,
  output [15:0] R5,
  output [15:0] R6,
  output [15:0] R7
);

  wire _0, _1, _2, _3, _4, _5, _6, _7, _8, _9, _10, _11, _12, _13, _14, _15, and_1_out, beq,
       bitselector_2_out, bne, branchornot_1_muxsel, clk, control_hazards_approach_1_jump, equal, EXMEMRead,
       hazard_detection_unit_1_update, hazard_detection_unit_1_write, ID_Flush, IF_Flush, INS, noStall,
       or_1_out, or_2_out, or_3_out, or_4_out, Regwrt_R, z_flagg;
  wire [1:0] ex_dm_reg_1_ex_dm_ctrl_2_2, FORWARDA, FORWARDB, jr_jalr;
  wire [2:0] ALuOp, controlunit_1_flush, ex_dm_reg_1_ex_dm_ctrl_2, multiplexer_6_out, Rd1, Rd2, Rd3, RS_F,
       RT_F;
  wire [3:0] ALU_ctrl;
  wire [4:0] DM_ctrl;
  wire [5:0] offset_R;
  wire [11:0] adder_1_out, bit_extender_1_out, bit_extender_7_out, control_hazards_approach_1_pctarget, Ctrl,
       Ctrl_Ex, id_ex_reg_1_ex_ctrl_signals_2, if_id_reg_1_n_pc_2, multiplexer_1_out, multiplexer_2_out,
       register_1_q;
  wire [15:0] ALU_F, ALU_R, bit_extender_4_out, BUS_B, Data_F, Data_WRT, Data_WRT_t,
       ex_dm_reg_1_alu_result_2, ex_dm_reg_1_bus_b_2, ex_dm_reg_1_n_pc_2, id_ex_reg_1_a_2, id_ex_reg_1_b_2,
       id_ex_reg_1_imm_2, Imm, jr, LUI1, LUI2, LUI3, multiplexer_4_out, multiplexer_7_out, N_PC, N_PC1,
       pc_plusOne, ram_1_data, Reg2, rom_1_data;

  Multiplexer #(.width(12), .enable("false")) multiplexer_1 (
    .in0(adder_1_out), .in1(control_hazards_approach_1_pctarget), .out(multiplexer_1_out),
    .sel(branchornot_1_muxsel));
  branchOrNot branchornot_1 (
    .J(control_hazards_approach_1_jump), .zero_flag(equal), .bne(bne), .beq(beq),
    .MUXSel(branchornot_1_muxsel));
  Bit_Extender #(.in_width(16), .out_width(12)) bit_extender_1 (.in(jr), .out(bit_extender_1_out));
  Register #(.width(12)) register_1 (
    .D(multiplexer_1_out), .en(hazard_detection_unit_1_update), .Q(register_1_q), .clk(clk));  // open: clr
  Adder #(.width(12)) adder_1 (.a(register_1_q), .b(12'h1), .out(adder_1_out));  // open: cin, cout
  Multiplexer #(.width(12), .enable("false")) multiplexer_2 (
    .in0({_11, _10, _9, _8, _7, _6, _5, _4, _3, _2, _1, _0}), .in1(bit_extender_1_out),
    .out(multiplexer_2_out), .sel(or_1_out));
  or or_1 (or_1_out, jr_jalr[0], jr_jalr[1]);
  assign pc_plusOne = {{4{1'b0}}, adder_1_out};  // Bit_Extender bit_extender_2
  ROM #(.addrWidth(12), .dataWidth(16)) rom_1 (.addr(register_1_q), .data(rom_1_data));  // open: sel
  Control_Hazards_Approach control_hazards_approach_1 (
    .Flush(controlunit_1_flush), .Target(multiplexer_2_out), .NPC(if_id_reg_1_n_pc_2),
    .Offset({_5, _4, _3, _2, _1, _0}), .FlushALL(ID_Flush), .Flush_IF(IF_Flush),
    .PCTarget(control_hazards_approach_1_pctarget), .jump(control_hazards_approach_1_jump),
    .DoFlush(branchornot_1_muxsel));
  or or_2 (or_2_out, IF_Flush, ID_Flush);
  Hazard_Detection_Unit hazard_detection_unit_1 (
    .PreviousRt(RT_F), .CurrentRs({_11, _10, _9}), .CurrentRt({_8, _7, _6}), .MemRead(EXMEMRead),
    .Write(hazard_detection_unit_1_write), .Update(hazard_detection_unit_1_update), .MUXSel(noStall));
  IF_ID_Reg if_id_reg_1 (
    .clk(clk), .Inst(rom_1_data), .N_Pc(adder_1_out),
    .Inst_2({_15, _14, _13, _12, _11, _10, _9, _8, _7, _6, _5, _4, _3, _2, _1, _0}),
    .N_Pc_2(if_id_reg_1_n_pc_2), .IF_ID_Wrt(hazard_detection_unit_1_write), .IF_Flush(or_2_out));
  assign N_PC = {{4{1'b0}}, if_id_reg_1_n_pc_2};  // Bit_Extender bit_extender_3
  nor nor_1 (INS, _15, _14, _13, _12, _11, _10, _8, _7, _6, _5, _4, _3, _2, _1, _0, _9);
  Comparator #(.width(16)) comparator_1 (.a(jr), .b(Reg2), .eq(equal));  // open: gt, lt
  Jout2 jout2_1 (.Op({_15, _14, _13, _12}), .Func({_2, _1, _0}), .JRJAR(jr_jalr));
  assign bit_extender_4_out = {{4{1'b0}}, {_11, _10, _9, _8, _7, _6, _5, _4, _3, _2, _1, _0}};  // Bit_Extender bit_extender_4
  assign Imm = {{10{_5}}, {_5, _4, _3, _2, _1, _0}};  // Bit_Extender bit_extender_5
  Shifter #(.width(16)) shifter_1 (.in(bit_extender_4_out), .\dist (4'b0100), .out(LUI1));
  RegisterFile registerfile_1 (
    .clk(clk), .Data(Data_WRT), .Write(Regwrt_R), .Rd(Rd3), .BusA(jr), .A({_11, _10, _9}), .BusB(Reg2),
    .B({_8, _7, _6}), .R0(R0), .R1(R1), .R2(R2), .R3(R3), .R4(R4), .R5(R5), .R6(R6), .R7(R7));
  ALUControlUnit alucontrolunit_1 (.Func({_2, _1, _0}), .ALUOp(ALuOp), .Code(ALU_ctrl));
  ControlUnit controlunit_1 (
    .OP({_15, _14, _13, _12}), .Rd(Ctrl[9:8]), .sec(Ctrl[0]), .JRJALR(jr_jalr), .Dest(Ctrl[11:10]),
    .ALUOP(ALuOp), .beq(beq), .bne(bne), .MemWrt(Ctrl[5]), .MemRead(Ctrl[6]), .RegWrt(Ctrl[7]),
    .Flush(controlunit_1_flush));  // open: PC2
  ID_EX_Reg id_ex_reg_1 (
    .clk(clk), .A(jr), .B(Reg2), .Rd1({_5, _4, _3}), .Imm(Imm), .EX_ctrl_signals(Ctrl_Ex),
    .A_2(id_ex_reg_1_a_2), .B_2(id_ex_reg_1_b_2), .Rd1_2(Rd1), .Imm_2(id_ex_reg_1_imm_2),
    .EX_ctrl_signals_2({id_ex_reg_1_ex_ctrl_signals_2[11:10], DM_ctrl, id_ex_reg_1_ex_ctrl_signals_2[4:0]}),
    .N_PC(N_PC), .N_PC_2(N_PC1), .LUI(LUI1), .LUI_2(LUI2), .Rs({_11, _10, _9}), .Rt({_8, _7, _6}),
    .Rs_2(RS_F), .Rt_2(RT_F));
  or or_3 (or_3_out, ~noStall, ID_Flush);  // OR_Gate
  Bit_Extender #(.in_width(16), .out_width(6)) bit_extender_6 (.in(id_ex_reg_1_imm_2), .out(offset_R));
  Multiplexer #(.width(12), .enable("false")) multiplexer_3 (
    .in0({Ctrl[11:5], ALU_ctrl, Ctrl[0]}), .in1({12{1'b0}}), .out(Ctrl_Ex), .sel(or_4_out));
  or or_4 (or_4_out, or_3_out, INS);
  Multiplexer #(.select(2), .width(16), .enable("false")) multiplexer_4 (
    .in0(id_ex_reg_1_a_2), .in1(ALU_R), .in2(Data_WRT_t), .out(multiplexer_4_out), .sel(FORWARDA));  // open: in3
  Multiplexer #(.select(2), .width(16), .enable("false")) multiplexer_5 (
    .in0(id_ex_reg_1_b_2), .in1(ALU_R), .in2(Data_WRT_t), .out(BUS_B), .sel(FORWARDB));  // open: in3
  Multiplexer #(.select(2), .width(3), .enable("false")) multiplexer_6 (
    .in0(RT_F), .in1(3'b001), .in2(3'b111), .in3(Rd1), .out(multiplexer_6_out),
    .sel(id_ex_reg_1_ex_ctrl_signals_2[11:10]));
  Multiplexer #(.width(16), .enable("false")) multiplexer_7 (
    .in0(BUS_B), .in1(id_ex_reg_1_imm_2), .out(multiplexer_7_out), .sel(id_ex_reg_1_ex_ctrl_signals_2[0]));
  BitSelector #(.width(5)) bitselector_1 (.in(DM_ctrl), .out(EXMEMRead), .sel(3'b001));
  ALU alu_1 (
    .in_1(multiplexer_4_out), .in_2(multiplexer_7_out), .Code(id_ex_reg_1_ex_ctrl_signals_2[4:1]),
    .out_4(ALU_F), .zeroFlag(z_flagg));
  Clock clock_1 (.out(clk));
  EX_DM_Reg ex_dm_reg_1 (
    .clk(clk), .ALU_Result(ALU_F), .Rd2(multiplexer_6_out), .Bus_B(BUS_B),
    .ALU_Result_2(ex_dm_reg_1_alu_result_2), .Rd2_2(Rd2), .Bus_B_2(ex_dm_reg_1_bus_b_2),
    .EX_Dm_ctrl_2({ex_dm_reg_1_ex_dm_ctrl_2_2, ex_dm_reg_1_ex_dm_ctrl_2}), .EX_Dm_ctrl(DM_ctrl),
    .N_PC(N_PC1), .N_PC_2(ex_dm_reg_1_n_pc_2), .LUI(LUI2), .LUI_2(LUI3));
  and and_1 (and_1_out, ex_dm_reg_1_ex_dm_ctrl_2_2[1], ex_dm_reg_1_ex_dm_ctrl_2_2[0]);
  Multiplexer #(.width(16), .enable("false")) multiplexer_8 (
    .in0(ex_dm_reg_1_alu_result_2), .in1(LUI3), .out(ALU_R), .sel(and_1_out));
  Bit_Extender #(.in_width(16), .out_width(12)) bit_extender_7 (
    .in(ex_dm_reg_1_alu_result_2), .out(bit_extender_7_out));
  BitSelector #(.width(5)) bitselector_2 (.in(DM_ctrl), .out(bitselector_2_out), .sel(3'b010));
  RAM #(.addrWidth(12), .dataWidth(16), .bus("separate")) ram_1 (
    .addr(bit_extender_7_out), .din(ex_dm_reg_1_bus_b_2), .data(ram_1_data),
    .str(ex_dm_reg_1_ex_dm_ctrl_2[0]), .clk(clk), .ld(ex_dm_reg_1_ex_dm_ctrl_2[1]));  // open: sel, clr
  Hazard_Detect_Forward_and_Stall hazard_detect_forward_and_stall_1 (
    .EX_MEM_REG_RD(Rd2), .EX_MEM_REG_WR(bitselector_2_out), .ID_EX_REG_RT(RT_F), .MEM_WB_REG_RD(Rd3),
    .MEM_WB_REG_WR(ex_dm_reg_1_ex_dm_ctrl_2[2]), .FORWARDA(FORWARDA), .out_8(FORWARDB), .ID_EX_REG_RS(RS_F));
  Multiplexer #(.select(2), .width(16), .enable("false")) multiplexer_9 (
    .in0(ram_1_data), .in1(ex_dm_reg_1_n_pc_2), .in2(ALU_R), .in3(LUI3), .out(Data_F),
    .sel(ex_dm_reg_1_ex_dm_ctrl_2_2));
  DM_WB_Reg dm_wb_reg_1 (
    .clk(clk), .Data_Wrt(Data_F), .Rd3(Rd2), .Reg_wrt(ex_dm_reg_1_ex_dm_ctrl_2[2]), .Data_Wrt_2(Data_WRT),
    .Rd3_2(Rd3), .Reg_wrt_2(Regwrt_R));

  // Other names for the same wires on the sheet: Ctrl[4:1] = ALU_ctrl; Rd[1:0] = Ctrl[9:8]; Dest[1:0] = Ctrl[11:10];
  //   Reg1[15:0] = jr; jump[11:0] = {_11, _10, _9, _8, _7, _6, _5, _4, _3, _2, _1, _0};
  //   offset[5:0] = {_5, _4, _3, _2, _1, _0}; Rd0[2:0] = {_5, _4, _3}; RT[2:0] = {_8, _7, _6};
  //   RS[2:0] = {_11, _10, _9}

  // Notes on the sheet:
  //   contents of rom_1 (hex, n*v repeats v):
  //   a384 8354 35b 2040 2081 20c2 890a 1921 4 1520 14f2 4 4 4 4183 1290 4 4037 3100 b017 55c 1b68 403f
  //   4e9 2040 4 2285 4 22c6 4 4e0 4 3100 1e06
endmodule

// Forward Unit
module Hazard_Detect_Forward_and_Stall (
  input  [2:0] ID_EX_REG_RS,
  input  [2:0] EX_MEM_REG_RD,
  input  EX_MEM_REG_WR,
  input  [2:0] ID_EX_REG_RT,
  input  [2:0] MEM_WB_REG_RD,
  input  MEM_WB_REG_WR,
  output [1:0] FORWARDA,
  output [1:0] out_8
);

  wire and_1_out, and_2_out, comparator_1_eq, comparator_2_eq, comparator_3_eq, comparator_4_eq,
       comparator_5_eq, comparator_6_eq, not_1_out, not_2_out;

  Comparator #(.width(3), .mode("unsigned")) comparator_1 (
    .a(EX_MEM_REG_RD), .b(3'b000), .eq(comparator_1_eq));  // open: gt, lt
  not not_1 (not_1_out, comparator_1_eq);
  Comparator #(.width(3)) comparator_2 (.a(EX_MEM_REG_RD), .b(ID_EX_REG_RT), .eq(comparator_2_eq));  // open: gt, lt
  Comparator #(.width(3), .mode("unsigned")) comparator_3 (
    .a(MEM_WB_REG_RD), .b(3'b000), .eq(comparator_3_eq));  // open: gt, lt
  Comparator #(.width(3)) comparator_4 (.a(ID_EX_REG_RS), .b(EX_MEM_REG_RD), .eq(comparator_4_eq));  // open: gt, lt
  and and_1 (and_1_out, not_1_out, EX_MEM_REG_WR);
  Comparator #(.width(3)) comparator_5 (.a(ID_EX_REG_RS), .b(MEM_WB_REG_RD), .eq(comparator_5_eq));  // open: gt, lt
  not not_2 (not_2_out, comparator_3_eq);
  and and_2 (and_2_out, not_2_out, MEM_WB_REG_WR);
  Comparator #(.width(3)) comparator_6 (.a(MEM_WB_REG_RD), .b(ID_EX_REG_RT), .eq(comparator_6_eq));  // open: gt, lt
  and and_3 (FORWARDA[0], comparator_4_eq, and_1_out);
  and and_4 (out_8[0], and_1_out, comparator_2_eq);
  and and_5 (FORWARDA[1], comparator_5_eq, and_2_out);
  and and_6 (out_8[1], and_2_out, comparator_6_eq);

  // Other names for the same wires on the sheet: FORWARDA_01 = FORWARDA[0]; FORWARDB_01 = out_8[0];
  //   RS[2:0] = ID_EX_REG_RS; RT[2:0] = ID_EX_REG_RT

  // Notes on the sheet:
  //   FORWARDB=10
  //   FORWARDA=10
endmodule

// BranchOrNot
module branchOrNot (
  input  J,
  input  zero_flag,
  input  bne,
  input  beq,
  output MUXSel
);

  wire and_1_out, and_2_out, or_1_out;

  or or_1 (or_1_out, and_1_out, and_2_out);
  and and_1 (and_1_out, ~zero_flag, bne);  // AND_Gate
  and and_2 (and_2_out, zero_flag, beq);
  or or_2 (MUXSel, J, or_1_out);

  // Notes on the sheet:
  //   BR
endmodule

module Hazard_Detection_Unit (
  input  [2:0] PreviousRt,
  input  [2:0] CurrentRs,
  input  [2:0] CurrentRt,
  input  MemRead,
  output Write,
  output Update,
  output MUXSel
);

  wire and_1_out, comparator_1_eq, comparator_2_eq, nor_1_out, or_1_out;

  nor nor_1 (nor_1_out, PreviousRt[0], PreviousRt[1], PreviousRt[2]);
  Comparator #(.width(3)) comparator_1 (.a(CurrentRs), .b(PreviousRt), .eq(comparator_1_eq));  // open: gt, lt
  Comparator #(.width(3)) comparator_2 (.a(CurrentRt), .b(PreviousRt), .eq(comparator_2_eq));  // open: gt, lt
  or or_1 (or_1_out, comparator_1_eq, comparator_2_eq);
  and and_1 (and_1_out, or_1_out, ~nor_1_out, MemRead);  // AND_Gate
  not not_1 (MUXSel, and_1_out);

  assign Update = MUXSel;
  assign Write = MUXSel;
endmodule

module flushing (
  input  [3:0] OP,
  input  [3:0] JR,
  input  [3:0] JALR,
  output [2:0] Flush
);

  wire comparator_1_eq, comparator_2_eq, comparator_3_eq, comparator_4_eq, comparator_5_eq, comparator_6_eq,
       or_1_out, or_2_out, or_3_out, or_4_out;
  wire [3:0] and_1_out, and_2_out;

  assign and_1_out = JR & 4'b0001;  // AND_Gate and_1, 4 bits wide
  assign and_2_out = JALR & 4'b0001;  // AND_Gate and_2, 4 bits wide
  or or_1 (or_1_out, OP[0], OP[1], OP[2], OP[3]);
  Comparator #(.width(4)) comparator_1 (.a(OP), .b(4'b1001), .eq(comparator_1_eq));  // open: gt, lt
  Comparator #(.width(4)) comparator_2 (.a(OP), .b(4'b0100), .eq(comparator_2_eq));  // open: gt, lt
  Comparator #(.width(4)) comparator_3 (.a(OP), .b(4'b0101), .eq(comparator_3_eq));  // open: gt, lt
  Comparator #(.width(4)) comparator_4 (.a(OP), .b(and_1_out), .eq(comparator_4_eq));  // open: gt, lt
  Comparator #(.width(4)) comparator_5 (.a(OP), .b(and_2_out), .eq(comparator_5_eq));  // open: gt, lt
  Comparator #(.width(4)) comparator_6 (.a(OP), .b(4'b1011), .eq(comparator_6_eq));  // open: gt, lt
  or or_2 (or_2_out, comparator_1_eq, comparator_2_eq, comparator_3_eq, comparator_4_eq);
  or or_3 (or_3_out, comparator_5_eq, comparator_6_eq);
  or or_4 (or_4_out, comparator_1_eq, comparator_4_eq, comparator_5_eq, comparator_6_eq);
  and and_3 (Flush[2], or_1_out, or_4_out);
  and and_4 (Flush[0], or_1_out, or_2_out);
  and and_5 (Flush[1], or_1_out, or_3_out);
endmodule

// Control Hazard
module Control_Hazards_Approach (
  input  DoFlush,
  input  [2:0] Flush,
  input  [11:0] Target,
  input  [11:0] NPC,
  input  [5:0] Offset,
  output FlushALL,
  output Flush_IF,
  output [11:0] PCTarget,
  output jump
);

  wire not_1_out;
  wire [11:0] adder_1_out, bit_extender_1_out;

  assign bit_extender_1_out = {{6{Offset[5]}}, Offset};  // Bit_Extender bit_extender_1
  Adder #(.width(12)) adder_1 (.a(NPC), .b(bit_extender_1_out), .out(adder_1_out));  // open: cin, cout
  Multiplexer #(.width(12), .enable("false")) multiplexer_1 (
    .in0(Target), .in1(adder_1_out), .out(PCTarget), .sel(not_1_out));
  not not_1 (not_1_out, Flush[2]);
  and and_1 (FlushALL, DoFlush, Flush[0]);
  and and_2 (Flush_IF, DoFlush, Flush[1]);

  assign jump = Flush[2];
endmodule
